// Digital circuit 8-bit-memory2.dig as structural Verilog
module _8_bit_memory2 (
  input  [2:0] Address_pin,
  input  [7:0] Data_input,
  input  CLK,
  input  [1:0] CTRL,
  output [7:0] Output
);

  wire and_1_out, and_2_out, and_3_out, and_4_out, and_5_out, and_6_out, and_7_out, and_8_out,
       decoder_1_out_0, decoder_1_out_1, decoder_1_out_2, decoder_1_out_3, decoder_1_out_4, decoder_1_out_5,
       decoder_1_out_6, decoder_1_out_7;
  wire [7:0] _8_bit_register_1_output, _8_bit_register_2_output, _8_bit_register_3_output,
       _8_bit_register_4_output, _8_bit_register_5_output, _8_bit_register_6_output,
       _8_bit_register_7_output, _8_bit_register_8_output;

  Decoder #(.Selector_Bits(3)) decoder_1 (
    .sel(Address_pin), .out_0(decoder_1_out_0), .out_1(decoder_1_out_1), .out_2(decoder_1_out_2),
    .out_3(decoder_1_out_3), .out_4(decoder_1_out_4), .out_5(decoder_1_out_5), .out_6(decoder_1_out_6),
    .out_7(decoder_1_out_7));
  and and_1 (and_1_out, CLK, decoder_1_out_0);
  and and_2 (and_2_out, CLK, decoder_1_out_1);
  and and_3 (and_3_out, CLK, decoder_1_out_2);
  and and_4 (and_4_out, CLK, decoder_1_out_3);
  and and_5 (and_5_out, CLK, decoder_1_out_4);
  and and_6 (and_6_out, CLK, decoder_1_out_5);
  and and_7 (and_7_out, CLK, decoder_1_out_6);
  and and_8 (and_8_out, CLK, decoder_1_out_7);
  _8_bit_register _8_bit_register_1 (
    .CLK(and_1_out), .Input(Data_input), .CTRL(CTRL), .Output(_8_bit_register_1_output));
  _8_bit_register _8_bit_register_2 (
    .CLK(and_2_out), .Input(Data_input), .CTRL(CTRL), .Output(_8_bit_register_2_output));
  _8_bit_register _8_bit_register_3 (
    .CLK(and_3_out), .Input(Data_input), .CTRL(CTRL), .Output(_8_bit_register_3_output));
  _8_bit_register _8_bit_register_4 (
    .CLK(and_4_out), .Input(Data_input), .CTRL(CTRL), .Output(_8_bit_register_4_output));
  _8_bit_register _8_bit_register_5 (
    .CLK(and_5_out), .Input(Data_input), .CTRL(CTRL), .Output(_8_bit_register_5_output));
  _8_bit_register _8_bit_register_6 (
    .CLK(and_6_out), .Input(Data_input), .CTRL(CTRL), .Output(_8_bit_register_6_output));
  _8_bit_register _8_bit_register_7 (
    .CLK(and_7_out), .Input(Data_input), .CTRL(CTRL), .Output(_8_bit_register_7_output));
  _8_bit_register _8_bit_register_8 (
    .CLK(and_8_out), .Input(Data_input), .CTRL(CTRL), .Output(_8_bit_register_8_output));
  Multiplexer #(.Selector_Bits(3), .Bits(8)) multiplexer_1 (
    .sel(Address_pin), .in_0(_8_bit_register_1_output), .in_1(_8_bit_register_2_output),
    .in_2(_8_bit_register_3_output), .in_3(_8_bit_register_4_output), .in_4(_8_bit_register_5_output),
    .in_5(_8_bit_register_6_output), .in_6(_8_bit_register_7_output), .in_7(_8_bit_register_8_output),
    .out(Output));
endmodule
