// Digital circuit control-unit.dig as structural Verilog
module control_unit (
  input  clk,
  output Inst_Execute,
  output Inst_Decode,
  output Inst_Fetch,
  output Write_Back
);

  D_FF #(.Default(1)) d_ff_1 (.D(Inst_Execute), .C(clk), .Q(Write_Back));  // open: nQ
  D_FF d_ff_2 (.D(Inst_Decode), .C(clk), .Q(Inst_Execute));  // open: nQ
  D_FF d_ff_3 (.D(Inst_Fetch), .C(clk), .Q(Inst_Decode));  // open: nQ
  D_FF d_ff_4 (.D(Write_Back), .C(clk), .Q(Inst_Fetch));  // open: nQ
endmodule
